# Fritzing sketch TrainMicro (saved by Fritzing 0.8.7b)
circuit board: 8.46667cm x 5.64444cm

parts:
  Part1 = Arduino Mega 2560 (Rev3)
  IC1 = ULN2003A [package="SO16 [SMD]"]
  IC2 = ULN2003A [package="SO16 [SMD]"]
  U1 = Optocoupler [package=THT]
  U2 = Optocoupler [package=THT]
  U3 = Optocoupler [package=THT]
  R1 = Resistor [tolerance=±5% resistance=1k package=THT]
  R2 = Resistor [tolerance=±5% resistance=1k package=THT]
  JP1 = Header 8 [package=1x08_smd]
  JP2 = Header 8 [package=1x08_smd]
  U4 = Optocoupler [package=THT]
  R3 = Resistor [tolerance=±5% resistance=1k package=THT]
  R4 = Resistor [tolerance=±5% resistance=1k package=THT]
  U5 = Optocoupler [package=THT]
  U6 = Optocoupler [package=THT]
  R5 = Resistor [tolerance=±5% resistance=1k package=THT]
  R6 = Resistor [tolerance=±5% resistance=1k package=THT]
  JP3 = Header 8 [package=1x08_smd]
  JP4 = Header 4 [package=1x04-smd]
  R7 = Resistor [tolerance=±5% resistance=1k package=THT]
  R8 = Resistor [tolerance=±5% resistance=1k package=THT]
  JP5 = Header 6 [package=1x06-smd]
  U7 = Optocoupler [package=THT]
  U8 = Optocoupler [package=THT]
  R9 = Resistor [tolerance=±5% resistance=1k package=THT]
  R10 = Resistor [tolerance=±5% resistance=1k package=THT]
  JP6 = Header 4 [package=1x04-smd]
  JP7 = Header 8 [package=1x08_smd]
  U9 = MAX485 [package=dil08]
  U10 = MAX485 [package=dil08]
  JP8 = Header 5 [package=1x05-1mm-ra]
  JP9 = Header 3 [package=1x03-1mm-ra]

nets:
  N1: Part1.A0, JP4.4, R8.Pin_0
  N2: Part1.A1, JP4.2, R7.Pin_0
  N3: Part1.D19/RX1, U10.RO
  N4: Part1.D18/TX1, U9.DI
  N5: Part1.SCL, JP5.4
  N6: Part1.SDA, JP5.6
  GND: Part1.GND, IC1.0V, IC2.0V, U1.Pin_2, U2.Pin_2, U3.Pin_2, JP1.8, JP2.8, U4.Pin_2, U5.Pin_2, U6.Pin_2, R7.Pin_1, R8.Pin_1, JP5.2, JP5.5, U7.Pin_2, U8.Pin_2, JP6.2, JP6.4, U9.GND, U10.RE, U10.DE, U10.GND, JP8.5, JP9.3
  N7: Part1.D22, IC1.In_1
  N8: Part1.D23, IC1.In_2
  N9: Part1.D24, IC1.In_3
  N10: Part1.D25, IC1.In_4
  N11: Part1.D26, IC1.In_5
  N12: Part1.D27, IC1.In_6
  N13: Part1.D28, IC1.In_7
  N14: Part1.D29, IC2.In_1
  N15: Part1.D30, IC2.In_2
  N16: Part1.D31, IC2.In_3
  N17: Part1.D32, IC2.In_4
  N18: Part1.D33, IC2.In_5
  N19: Part1.D34, IC2.In_6
  N20: Part1.D35, IC2.In_7
  N21: Part1.D36, R2.Pin_0
  N22: Part1.D37, R1.Pin_0
  N23: Part1.D38, R3.Pin_0
  N24: Part1.D39, R4.Pin_0
  N25: Part1.D40, R5.Pin_0
  N26: Part1.D41, R6.Pin_0
  N27: Part1.D42, R10.Pin_1
  N28: Part1.D43, R9.Pin_1
  N29: Part1.D47, JP7.8
  N30: Part1.D48, JP7.7
  N31: Part1.D49, JP7.6
  N32: Part1.D50, JP7.5
  N33: Part1.D51, JP7.4
  N34: Part1.D52, JP7.3
  N35: Part1.D53, JP7.2
  24V: IC1.COM_-_Common, IC2.COM_-_Common, U1.Pin_5, U2.Pin_5, U4.Pin_5, U5.Pin_5, U6.Pin_5, JP3.1, U7.Pin_5, U8.Pin_5
  N36: IC1.Out_7, JP1.7
  N37: IC1.Out_6, JP1.6
  N38: IC1.Out_5, JP1.5
  N39: IC1.Out_4, JP1.4
  N40: IC1.Out_3, JP1.3
  N41: IC1.Out_2, JP1.2
  N42: IC1.Out_1, JP1.1
  N43: IC2.Out_7, JP2.7
  N44: IC2.Out_6, JP2.6
  N45: IC2.Out_5, JP2.5
  N46: IC2.Out_4, JP2.4
  N47: IC2.Out_3, JP2.3
  N48: IC2.Out_2, JP2.2
  N49: IC2.Out_1, JP2.1
  N50: U1.Pin_1, R1.Pin_1
  N51: U1.Pin_4, JP3.7
  N52: U2.Pin_1, R3.Pin_1
  N53: U2.Pin_4, JP3.3
  N54: U3.Pin_1, R2.Pin_1
  N55: U3.Pin_4, JP3.8
  N56: U4.Pin_1, R4.Pin_1
  N57: U4.Pin_4, JP3.4
  N58: U5.Pin_1, R5.Pin_1
  N59: U5.Pin_4, JP3.5
  N60: U6.Pin_1, R6.Pin_1
  N61: U6.Pin_4, JP3.6
  5V: JP4.1, JP4.3, JP7.1, JP9.1
  VCC: JP5.1, JP5.3, U9.RE, U9.DE, U9.VCC, U10.VCC
  N62: U7.Pin_1, R9.Pin_0
  N63: U7.Pin_4, JP6.1
  N64: U8.Pin_1, R10.Pin_0
  N65: U8.Pin_4, JP6.3
  N66: U9.A, JP8.1
  N67: U9.B, JP8.2
  N68: U10.A, JP8.3
  N69: U10.B, JP8.4

notes:
  LED Out
  Relay Control 1
  Relay Control 2
  Speed Sense
  Thermistor In
  Traction Control
  Relay Input
  RS422 Coms
  5V Power
